# Fritzing sketch 图纸 (saved by Fritzing 0.9.5d)
breadboards: 1

parts:
  元件1 = Arduino Uno (Rev3)
  MCU1 = Raspberry Pi Zero

nets:
  N1: 元件1.D8, MCU1.pin_15
  N2: 元件1.D9_PWM, MCU1.pin_13
  N3: 元件1.D10_PWM/SS, MCU1.pin_12
  N4: 元件1.D11_PWM/MOSI, MCU1.pin_11
  N5: 元件1.GND, MCU1.pin_9, MCU1.pin_39
  N6: 元件1.D2, MCU1.pin_31
  N7: 元件1.D3_PWM, MCU1.pin_29
  N8: 元件1.D4, MCU1.pin_7
  N9: 元件1.D5_PWM, MCU1.pin_22
  N10: 元件1.D6_PWM, MCU1.pin_18
  N11: 元件1.D7, MCU1.pin_16
  N12: 元件1.3V3, MCU1.pin_1
